// Logisim project Singlecpu.circ as structural Verilog: 2 circuits, main circuit main
module main (
  input  [15:0] INSTRUCTION,
  input  CLOCK,
  output [15:0] FETCH_ADDRESS,
  output [15:0] s0_Value,
  output [15:0] s1_Value,
  output [15:0] s2_Value,
  output [15:0] ra_Value,
  output [15:0] sp_Value,
  output [15:0] HI_Value,
  output [15:0] LO_Value
);

  wire and_1_out, and_2_out, comparator_2_eq, comparator_3_eq, comparator_4_eq, comparator_5_eq,
       comparator_6_gt, comparator_7_eq, comparator_8_eq, comparator_9_eq, comparator_10_eq,
       comparator_11_eq, equal, Ex_ops, HiWrite, idk, Imm_Type, isU, jump, LoWrite, main_1_p4, main_1_p5,
       MEM_p1, MEM_p2, MEM_p4, MEM_p10, MemtoReg, Memwrite, moveHi, moveLo, not_1_out, or_2_out, or_3_out,
       regWrite, takeBranch, Type;
  wire [2:0] ALUsrc, bit_extender_4_out, multiplexer_2_out, multiplexer_4_out;
  wire [15:0] adder_1_out, adder_2_out, adder_3_out, adder_4_out, and_3_out, bit_extender_1_out,
       bit_extender_2_out, bit_extender_3_out, Imm, MemRead, multiplexer_1_out, multiplexer_5_out,
       multiplexer_6_out, multiplexer_7_out, multiplexer_8_out, multiplexer_9_out, multiplexer_10_out,
       multiplexer_11_out, multiplexer_12_out, multiplexer_13_out, multiplexer_14_out, multiplexer_15_out,
       R1, R2, ReadReg1, ReadReg2, shifter_1_out;

  Comparator #(.width(4), .mode("unsigned")) comparator_1 (
    .a(INSTRUCTION[15:12]), .b(4'b0001), .gt(idk));  // open: eq, lt
  Comparator #(.width(4), .mode("unsigned")) comparator_2 (
    .a(INSTRUCTION[15:12]), .b(4'b0100), .eq(comparator_2_eq));  // open: gt, lt
  Comparator #(.width(4), .mode("unsigned")) comparator_3 (
    .a(INSTRUCTION[15:12]), .b(4'b0101), .eq(comparator_3_eq));  // open: gt, lt
  assign bit_extender_1_out = {{10{INSTRUCTION[5]}}, INSTRUCTION[5:0]};  // Bit_Extender bit_extender_1
  assign bit_extender_2_out = {{10{1'b0}}, INSTRUCTION[5:0]};  // Bit_Extender bit_extender_2
  and and_1 (and_1_out, equal, comparator_2_eq);
  not not_1 (not_1_out, equal);
  and and_2 (and_2_out, not_1_out, comparator_3_eq);
  Comparator #(.width(4), .mode("unsigned")) comparator_4 (
    .a(INSTRUCTION[15:12]), .b(4'b0010), .eq(comparator_4_eq));  // open: gt, lt
  Comparator #(.width(4), .mode("unsigned")) comparator_5 (
    .a(INSTRUCTION[15:12]), .b(4'b0011), .eq(comparator_5_eq));  // open: gt, lt
  assign bit_extender_3_out = {{6{INSTRUCTION[9]}}, INSTRUCTION[9:0]};  // Bit_Extender bit_extender_3
  Multiplexer #(.width(16)) multiplexer_1 (
    .in0(bit_extender_1_out), .in1(bit_extender_2_out), .out(multiplexer_1_out), .sel(Ex_ops));  // open: en
  or or_1 (takeBranch, and_1_out, and_2_out);
  Multiplexer #(.width(3)) multiplexer_2 (
    .in0(INSTRUCTION[11:9]), .in1(bit_extender_4_out), .out(multiplexer_2_out), .sel(isU));  // open: en
  assign bit_extender_4_out = {{1{1'b0}}, INSTRUCTION[11:10]};  // Bit_Extender bit_extender_4
  or or_2 (or_2_out, comparator_4_eq, comparator_5_eq);
  Comparator #(.width(4), .mode("unsigned")) comparator_6 (
    .a(INSTRUCTION[15:12]), .b(4'b1011), .gt(comparator_6_gt));  // open: eq, lt
  // Probe on R1
  Multiplexer #(.width(16)) multiplexer_3 (
    .in0(bit_extender_3_out), .in1(multiplexer_1_out), .out(Imm), .sel(Imm_Type));  // open: en
  // Probe on INSTRUCTION
  Multiplexer #(.width(3)) multiplexer_4 (
    .in0(INSTRUCTION[5:3]), .in1(INSTRUCTION[11:9]), .out(multiplexer_4_out), .sel(idk));  // open: en
  Multiplexer #(.width(16)) multiplexer_5 (
    .in0(R1), .in1(MemRead), .out(multiplexer_5_out), .sel(MemtoReg));  // open: en
  // Probe on LO_Value
  // Probe on Imm
  // Probe on INSTRUCTION[2:0]
  // Probe on multiplexer_6_out
  Multiplexer #(.width(16)) multiplexer_6 (
    .in0(multiplexer_7_out), .in1(adder_3_out), .out(multiplexer_6_out), .sel(or_2_out));  // open: en
  Multiplexer #(.width(16)) multiplexer_7 (
    .in0(multiplexer_5_out), .in1(multiplexer_8_out), .out(multiplexer_7_out), .sel(comparator_6_gt));  // open: en
  Multiplexer #(.width(16)) multiplexer_8 (
    .in0(LO_Value), .in1(HI_Value), .out(multiplexer_8_out), .sel(comparator_7_eq));  // open: en
  Comparator #(.width(4), .mode("unsigned")) comparator_7 (
    .a(INSTRUCTION[15:12]), .b(4'b1100), .eq(comparator_7_eq));  // open: gt, lt
  // Probe on INSTRUCTION[5:3]
  // Probe on INSTRUCTION[15:12]
  Multiplexer #(.width(16)) multiplexer_9 (
    .in0(16'h2), .in1(Imm), .out(multiplexer_9_out), .sel(takeBranch));  // open: en
  assign and_3_out = 16'hfc00 & FETCH_ADDRESS;  // AND_Gate and_3, 16 bits wide
  // regfile_main main_1: pin names not known; wires that end beside it: INSTRUCTION[8:6], multiplexer_4_out, multiplexer_2_out, main_1_p4, main_1_p5, s0_Value, multiplexer_6_out, s1_Value, regWrite, s2_Value, CLOCK, ra_Value, sp_Value, ReadReg1, ReadReg2
  Adder #(.width(16)) adder_1 (.a(FETCH_ADDRESS), .b(multiplexer_9_out), .out(adder_1_out));  // open: cin, cout
  Adder #(.width(16)) adder_2 (.a(and_3_out), .b(Imm), .out(adder_2_out));  // open: cin, cout
  Multiplexer #(.width(16)) multiplexer_10 (
    .in0(HI_Value), .in1(R2), .out(multiplexer_10_out), .sel(HiWrite));  // open: en
  Multiplexer #(.width(16)) multiplexer_11 (
    .in0(adder_1_out), .in1(multiplexer_12_out), .out(multiplexer_11_out), .sel(or_3_out));  // open: en
  // Probe on multiplexer_12_out
  Multiplexer #(.width(16)) multiplexer_12 (
    .in0(adder_2_out), .in1(R1), .out(multiplexer_12_out), .sel(comparator_8_eq));  // open: en
  Comparator #(.width(4), .mode("unsigned")) comparator_8 (
    .a(INSTRUCTION[15:12]), .b(4'b0011), .eq(comparator_8_eq));  // open: gt, lt
  Adder #(.width(16)) adder_3 (.a(FETCH_ADDRESS), .b(16'h2), .out(adder_3_out));  // open: cin, cout
  Register #(.width(16)) HI (.D(multiplexer_10_out), .Q(HI_Value), .clk(CLOCK));  // open: en, clr
  control control_1 (
    .Funct(INSTRUCTION[2:0]), .Opcode(INSTRUCTION[15:12]), .RegWrite(regWrite), .MemtoReg(MemtoReg),
    .MemWrite(Memwrite), .Type(Type), .Hi(HiWrite), .Lo(LoWrite), .Move_Hi(moveHi), .Move_Lo(moveLo),
    .ALUSrc(ALUsrc), .isU(isU), .Imm_type(Imm_Type), .Ex_Ops(Ex_ops), .Jump(jump));
  Register #(.width(16)) Pc (.D(multiplexer_11_out), .Q(FETCH_ADDRESS), .clk(CLOCK));  // open: en, clr
  Comparator #(.width(4), .mode("unsigned")) comparator_9 (
    .a(INSTRUCTION[15:12]), .b(4'b0010), .eq(comparator_9_eq));  // open: gt, lt
  Comparator #(.width(4), .mode("unsigned")) comparator_10 (
    .a(INSTRUCTION[15:12]), .b(4'b0011), .eq(comparator_10_eq));  // open: gt, lt
  or or_3 (or_3_out, comparator_9_eq, comparator_10_eq);
  Multiplexer #(.width(16)) multiplexer_13 (
    .in0(R1), .in1(shifter_1_out), .out(multiplexer_13_out), .sel(comparator_11_eq));  // open: en
  Shifter #(.width(16)) shifter_1 (.in(Imm), .\dist (4'b0110), .out(shifter_1_out));
  Comparator #(.width(4), .mode("unsigned")) comparator_11 (
    .a(INSTRUCTION[15:12]), .b(4'b0001), .eq(comparator_11_eq));  // open: gt, lt
  Adder #(.width(16)) adder_4 (.a(ReadReg1), .b(Imm), .out(adder_4_out));  // open: cin, cout
  Multiplexer #(.width(16)) multiplexer_14 (
    .in0(ReadReg2), .in1(Imm), .out(multiplexer_14_out), .sel(Type));  // open: en
  Multiplexer #(.width(16)) multiplexer_15 (
    .in0(LO_Value), .in1(multiplexer_13_out), .out(multiplexer_15_out), .sel(LoWrite));  // open: en
  // mem_main MEM: pin names not known; wires that end beside it: MEM_p1, MEM_p2, MEM_p2, MEM_p4, adder_4_out, ReadReg2, Memwrite, MEM_p4, CLOCK, MEM_p10, MemRead
  // alu_main main_2: pin names not known; wires that end beside it: ReadReg1, multiplexer_14_out, ALUsrc, equal, R1, R2
  Register #(.width(16)) LO (.D(multiplexer_15_out), .Q(LO_Value), .clk(CLOCK));  // open: en, clr

  // Other names for the same wires on the sheet: clk = CLOCK; HI[15:0] = HI_Value; funct[2:0] = INSTRUCTION[2:0];
  //   IImm[5:0] = INSTRUCTION[5:0]; UImm[9:0] = INSTRUCTION[9:0]; rt[2:0] = INSTRUCTION[5:3];
  //   rs[2:0] = INSTRUCTION[8:6]; rd[2:0] = INSTRUCTION[11:9]; Urd[1:0] = INSTRUCTION[11:10];
  //   opcode[3:0] = INSTRUCTION[15:12]; LO[15:0] = LO_Value; Pc[15:0] = FETCH_ADDRESS; ra[15:0] = ra_Value;
  //   s0[15:0] = s0_Value; s1[15:0] = s1_Value; s2[15:0] = s2_Value; sp[15:0] = sp_Value

  // Notes on the sheet:
  //   Output
  //   These are outputs/inputs from run.circ
  //   Inputs
  //   These are DEBUG/TEST outputs from your circuit.
endmodule

module control (
  input  [2:0] Funct,
  input  [3:0] Opcode,
  output Type,
  output RegWrite,
  output Hi,
  output Lo,
  output MemWrite,
  output MemtoReg,
  output Move_Hi,
  output Move_Lo,
  output isU,
  output [2:0] ALUSrc,
  output Imm_type,
  output Ex_Ops,
  output Jump
);

  wire and_1_out, and_5_out, and_6_out, comparator_1_eq, comparator_2_eq, comparator_3_eq, comparator_4_gt,
       comparator_5_lt, comparator_6_gt, comparator_7_lt, comparator_8_gt, comparator_9_lt, comparator_10_eq,
       comparator_11_eq, comparator_12_eq, comparator_13_eq, comparator_14_lt, comparator_15_gt,
       comparator_16_lt, comparator_17_eq, comparator_18_eq, comparator_19_eq, comparator_24_eq,
       comparator_25_eq, not_1_out, not_2_out, not_3_out, or_1_out, or_2_out, or_3_out;

  Comparator #(.width(4), .mode("unsigned")) comparator_1 (
    .a(Opcode), .b(4'b0100), .eq(comparator_1_eq));  // open: gt, lt
  Comparator #(.width(4), .mode("unsigned")) comparator_2 (
    .a(Opcode), .b(4'b0101), .eq(comparator_2_eq));  // open: gt, lt
  Comparator #(.width(4), .mode("unsigned")) comparator_3 (
    .a(Opcode), .b(4'b1011), .eq(comparator_3_eq));  // open: gt, lt
  Comparator #(.width(4), .mode("unsigned")) comparator_4 (
    .a(Opcode), .b(4'b0000), .gt(comparator_4_gt));  // open: eq, lt
  Comparator #(.width(4), .mode("unsigned")) comparator_5 (
    .a(Opcode), .b(4'b0011), .lt(comparator_5_lt));  // open: gt, eq
  Comparator #(.width(4), .mode("unsigned")) comparator_6 (
    .a(Opcode), .b(4'b1000), .gt(comparator_6_gt));  // open: eq, lt
  Comparator #(.width(4), .mode("unsigned")) comparator_7 (
    .a(Opcode), .b(4'b1001), .lt(comparator_7_lt));  // open: gt, eq
  Comparator #(.width(4), .mode("unsigned")) comparator_8 (
    .a(Opcode), .b(4'b0001), .gt(comparator_8_gt));  // open: eq, lt
  Comparator #(.width(4), .mode("unsigned")) comparator_9 (
    .a(Opcode), .b(4'b0100), .lt(comparator_9_lt));  // open: gt, eq
  Comparator #(.width(4), .mode("unsigned")) comparator_10 (
    .a(Opcode), .b(4'b0000), .eq(comparator_10_eq));  // open: gt, lt
  Comparator #(.width(4), .mode("unsigned")) comparator_11 (
    .a(Opcode), .b(4'b0100), .eq(comparator_11_eq));  // open: gt, lt
  Comparator #(.width(4), .mode("unsigned")) comparator_12 (
    .a(Opcode), .b(4'b0101), .eq(comparator_12_eq));  // open: gt, lt
  Comparator #(.width(4), .mode("unsigned")) comparator_13 (
    .a(Opcode), .b(4'b0000), .eq(comparator_13_eq));  // open: gt, lt
  Comparator #(.width(3), .mode("unsigned")) comparator_14 (
    .a(Funct), .b(3'b111), .lt(comparator_14_lt));  // open: gt, eq
  Comparator #(.width(4), .mode("unsigned")) comparator_15 (
    .a(Opcode), .b(4'b0001), .gt(comparator_15_gt));  // open: eq, lt
  Comparator #(.width(4), .mode("unsigned")) comparator_16 (
    .a(Opcode), .b(4'b1110), .lt(comparator_16_lt));  // open: gt, eq
  or or_1 (or_1_out, comparator_1_eq, comparator_2_eq, comparator_3_eq);
  Comparator #(.width(4), .mode("unsigned")) comparator_17 (
    .a(Opcode), .b(4'b0000), .eq(comparator_17_eq));  // open: gt, lt
  Comparator #(.width(3), .mode("unsigned")) comparator_18 (
    .a(Funct), .b(3'b111), .eq(comparator_18_eq));  // open: gt, lt
  Comparator #(.width(4), .mode("unsigned")) comparator_19 (
    .a(Opcode), .b(4'b0001), .eq(comparator_19_eq));  // open: gt, lt
  Comparator #(.width(4), .mode("unsigned")) comparator_20 (.a(Opcode), .b(4'b1011), .eq(MemWrite));  // open: gt, lt
  Comparator #(.width(4), .mode("unsigned")) comparator_21 (.a(Opcode), .b(4'b1010), .eq(MemtoReg));  // open: gt, lt
  Comparator #(.width(4), .mode("unsigned")) comparator_22 (.a(Opcode), .b(4'b1100), .eq(Move_Hi));  // open: gt, lt
  Comparator #(.width(4), .mode("unsigned")) comparator_23 (.a(Opcode), .b(4'b1101), .eq(Move_Lo));  // open: gt, lt
  Comparator #(.width(4), .mode("unsigned")) comparator_24 (
    .a(Opcode), .b(4'b0001), .eq(comparator_24_eq));  // open: gt, lt
  Comparator #(.width(4), .mode("unsigned")) comparator_25 (
    .a(Opcode), .b(4'b0010), .eq(comparator_25_eq));  // open: gt, lt
  Multiplexer #(.select(4), .width(3)) multiplexer_1 (
    .in0(Funct), .in1(3'b000), .in2(3'b010), .in3(3'b010), .in4(3'b010), .in5(3'b000), .in6(3'b010),
    .in7(3'b110), .in8(3'b011), .in9(3'b100), .in10(3'b000), .in11(3'b000), .in12(3'b000), .in13(3'b000),
    .in14(3'b000), .in15(3'b000), .out(ALUSrc), .sel(Opcode));  // open: en
  and and_1 (and_1_out, comparator_4_gt, comparator_5_lt);
  or or_2 (or_2_out, comparator_6_gt, comparator_7_lt);
  and and_2 (Jump, comparator_8_gt, comparator_9_lt);
  not not_1 (not_1_out, comparator_10_eq);
  not not_2 (not_2_out, or_3_out);
  or or_3 (or_3_out, comparator_11_eq, comparator_12_eq);
  not not_3 (not_3_out, or_1_out);
  and and_3 (Hi, comparator_17_eq, comparator_18_eq);
  or or_4 (Lo, Hi, comparator_19_eq);
  or or_5 (isU, comparator_24_eq, comparator_25_eq);
  not not_4 (Imm_type, and_1_out);
  not not_5 (Ex_Ops, or_2_out);
  and and_4 (Type, not_1_out, not_2_out);
  and and_5 (and_5_out, comparator_13_eq, comparator_14_lt);
  and and_6 (and_6_out, comparator_15_gt, comparator_16_lt, not_3_out);
  or or_6 (RegWrite, and_5_out, and_6_out);
endmodule
