// Logisim project alu3.circ as structural Verilog: 1 circuit, main circuit main
module main (
  input  [31:0] X,
  input  [31:0] Y,
  input  [3:0] Switch,
  output Signed_Overflow,
  output Equal,
  output [31:0] Result
);

  wire and_1_out, and_2_out, and_3_out, and_4_out, carryout, comparator_1_lt, comparator_2_lt;
  wire [4:0] bit_extender_1_out, bit_extender_2_out, bit_extender_3_out;
  wire [31:0] add, addu, \and , \or , sll, slr, slt, sltu, sra, sub, subu;

  Multiplexer #(.select(4), .width(32)) multiplexer_1 (
    .in0(sll), .in1(slr), .in2(sra), .in5(add), .in6(addu), .in7(sub), .in8(subu), .in9(\and ), .in10(\or ),
    .in11(slt), .in12(sltu), .out(Result), .sel(Switch));  // open: in3, in4, in13, in14, in15, en
  Multiplexer #(.select(4)) multiplexer_2 (
    .in0(1'b0), .in1(1'b0), .in2(1'b0), .in3(1'b0), .in4(1'b0), .in5(carryout), .in6(1'b0), .in7(carryout),
    .in8(1'b0), .in9(1'b0), .in10(1'b0), .in11(1'b0), .in12(1'b0), .in13(1'b0), .in14(1'b0), .in15(1'b0),
    .out(Signed_Overflow), .sel(Switch));  // open: en
  Bit_Extender #(.in_width(32), .out_width(5)) bit_extender_1 (.in(X), .out(bit_extender_1_out));
  Bit_Extender #(.in_width(32), .out_width(5)) bit_extender_2 (.in(X), .out(bit_extender_2_out));
  Bit_Extender #(.in_width(32), .out_width(5)) bit_extender_3 (.in(X), .out(bit_extender_3_out));
  Shifter #(.width(32)) shifter_1 (.in(Y), .\dist (bit_extender_1_out), .out(sll));
  Shifter #(.width(32), .shift("lr")) shifter_2 (.in(Y), .\dist (bit_extender_2_out), .out(slr));
  Shifter #(.width(32), .shift("ar")) shifter_3 (.in(Y), .\dist (bit_extender_3_out), .out(sra));
  Adder #(.width(32)) adder_1 (.a(X), .b(Y), .out(add));  // open: cin, cout
  Adder #(.width(32)) adder_2 (.a(X), .b(Y), .out(addu));  // open: cin, cout
  and and_1 (and_1_out, X[31], Y[31]);
  and and_2 (and_2_out, ~X[31], ~Y[31]);  // AND_Gate
  and and_3 (and_3_out, and_1_out, ~Result[31]);  // AND_Gate
  and and_4 (and_4_out, and_2_out, Result[31]);
  Subtractor #(.width(32)) subtractor_1 (.a(X), .b(Y), .out(sub));  // open: bin, bout
  Subtractor #(.width(32)) subtractor_2 (.a(X), .b(Y), .out(subu));  // open: bin, bout
  or or_1 (carryout, and_3_out, and_4_out);
  assign \and  = X & Y;  // AND_Gate and_5, 32 bits wide
  assign \or  = X | Y;  // OR_Gate or_2, 32 bits wide
  Comparator #(.width(32)) comparator_1 (.a(X), .b(Y), .lt(comparator_1_lt));  // open: gt, eq
  assign slt = {{31{1'b0}}, comparator_1_lt};  // Bit_Extender bit_extender_4
  Comparator #(.width(32), .mode("unsigned")) comparator_2 (
    .a(X), .b(Y), .eq(Equal), .lt(comparator_2_lt));  // open: gt
  assign sltu = {{31{1'b0}}, comparator_2_lt};  // Bit_Extender bit_extender_5

  // Other names for the same wires on the sheet: overflow = Signed_Overflow; S[3:0] = Switch

  // Notes on the sheet:
  //   INPUTS to your circuit
  //   DON'T CHANGE THE LOCATIONS OF THE INPUTS AND OUTPUTS!
  //   OUTPUTS from your circuit
endmodule
