// Logisim project regFile2.circ as structural Verilog: 1 circuit, main circuit main
module main (
  input  [4:0] Read_Register_1,
  input  [4:0] Read_Register_2,
  input  [4:0] Write_Register,
  input  [31:0] Write_Data,
  input  Write_Enable,
  input  Clock,
  output [31:0] s0_Value,
  output [31:0] s1_Value,
  output [31:0] s2_Value,
  output [31:0] ra_Value,
  output [31:0] sp_Value,
  output [31:0] Read_Data_1,
  output [31:0] Read_Data_2
);

  wire write_en_1, write_en_2, write_en_3, write_en_4, write_en_5, write_en_6, write_en_7, write_en_8,
       write_en_9, write_en_10, write_en_11, write_en_12, write_en_13, write_en_14, write_en_15, write_en_16,
       write_en_17, write_en_18, write_en_19, write_en_20, write_en_21, write_en_22, write_en_23,
       write_en_24, write_en_25, write_en_26, write_en_27, write_en_28, write_en_29, write_en_30, write_en_31;
  wire [31:0] a0, a1, a2, a3, at, fp, gp, k0, k1, s3, s4, s5, s6, s7, t0, t1, t2, t3, t4, t5, t6, t7, t8, t9,
       v0, v1;

  Demultiplexer #(.select(5)) demultiplexer_1 (
    .out1(write_en_1), .out2(write_en_2), .out3(write_en_3), .out4(write_en_4), .out5(write_en_5),
    .out6(write_en_6), .out7(write_en_7), .out8(write_en_8), .out9(write_en_9), .out10(write_en_10),
    .out11(write_en_11), .out12(write_en_12), .out13(write_en_13), .out14(write_en_14), .out15(write_en_15),
    .out16(write_en_16), .out17(write_en_17), .out18(write_en_18), .out19(write_en_19), .out20(write_en_20),
    .out21(write_en_21), .out22(write_en_22), .out23(write_en_23), .out24(write_en_24), .out25(write_en_25),
    .out26(write_en_26), .out27(write_en_27), .out28(write_en_28), .out29(write_en_29), .out30(write_en_30),
    .out31(write_en_31), .in(Write_Enable), .sel(Write_Register));  // open: out0, en
  Multiplexer #(.select(5), .width(32)) multiplexer_1 (
    .in0({32{1'b0}}), .in1(at), .in2(v0), .in3(v1), .in4(a0), .in5(a1), .in6(a2), .in7(a3), .in8(t0),
    .in9(t1), .in10(t2), .in11(t3), .in12(t4), .in13(t5), .in14(t6), .in15(t7), .in16(s0_Value),
    .in17(s1_Value), .in18(s2_Value), .in19(s3), .in20(s4), .in21(s5), .in22(s6), .in23(s7), .in24(t8),
    .in25(t9), .in26(k0), .in27(k1), .in28(gp), .in29(sp_Value), .in30(fp), .in31(ra_Value),
    .out(Read_Data_1), .sel(Read_Register_1));  // open: en
  Multiplexer #(.select(5), .width(32)) multiplexer_2 (
    .in0({32{1'b0}}), .in1(at), .in2(v0), .in3(v1), .in4(a0), .in5(a1), .in6(a2), .in7(a3), .in8(t0),
    .in9(t1), .in10(t2), .in11(t3), .in12(t4), .in13(t5), .in14(t6), .in15(t7), .in16(s0_Value),
    .in17(s1_Value), .in18(s2_Value), .in19(s3), .in20(s4), .in21(s5), .in22(s6), .in23(s7), .in24(t8),
    .in25(t9), .in26(k0), .in27(k1), .in28(gp), .in29(sp_Value), .in30(fp), .in31(ra_Value),
    .out(Read_Data_2), .sel(Read_Register_2));  // open: en
  Register #(.width(32)) register_1 (.D(Write_Data), .en(write_en_1), .Q(at), .clk(Clock));  // open: clr
  Register #(.width(32)) register_2 (.D(Write_Data), .en(write_en_2), .Q(v0), .clk(Clock));  // open: clr
  Register #(.width(32)) register_3 (.D(Write_Data), .en(write_en_3), .Q(v1), .clk(Clock));  // open: clr
  Register #(.width(32)) register_4 (.D(Write_Data), .en(write_en_4), .Q(a0), .clk(Clock));  // open: clr
  Register #(.width(32)) register_5 (.D(Write_Data), .en(write_en_5), .Q(a1), .clk(Clock));  // open: clr
  Register #(.width(32)) register_6 (.D(Write_Data), .en(write_en_6), .Q(a2), .clk(Clock));  // open: clr
  Register #(.width(32)) register_7 (.D(Write_Data), .en(write_en_7), .Q(a3), .clk(Clock));  // open: clr
  Register #(.width(32)) register_8 (.D(Write_Data), .en(write_en_8), .Q(t0), .clk(Clock));  // open: clr
  Register #(.width(32)) register_9 (.D(Write_Data), .en(write_en_9), .Q(t1), .clk(Clock));  // open: clr
  Register #(.width(32)) register_10 (.D(Write_Data), .en(write_en_10), .Q(t2), .clk(Clock));  // open: clr
  Register #(.width(32)) register_11 (.D(Write_Data), .en(write_en_11), .Q(t3), .clk(Clock));  // open: clr
  Register #(.width(32)) register_12 (.D(Write_Data), .en(write_en_12), .Q(t4), .clk(Clock));  // open: clr
  Register #(.width(32)) register_13 (.D(Write_Data), .en(write_en_13), .Q(t5), .clk(Clock));  // open: clr
  Register #(.width(32)) register_14 (.D(Write_Data), .en(write_en_14), .Q(t6), .clk(Clock));  // open: clr
  Register #(.width(32)) register_15 (.D(Write_Data), .en(write_en_15), .Q(t7), .clk(Clock));  // open: clr
  Register #(.width(32)) register_16 (.D(Write_Data), .en(write_en_16), .Q(s0_Value), .clk(Clock));  // open: clr
  Register #(.width(32)) register_17 (.D(Write_Data), .en(write_en_17), .Q(s1_Value), .clk(Clock));  // open: clr
  Register #(.width(32)) register_18 (.D(Write_Data), .en(write_en_18), .Q(s2_Value), .clk(Clock));  // open: clr
  Register #(.width(32)) register_19 (.D(Write_Data), .en(write_en_19), .Q(s3), .clk(Clock));  // open: clr
  Register #(.width(32)) register_20 (.D(Write_Data), .en(write_en_20), .Q(s4), .clk(Clock));  // open: clr
  Register #(.width(32)) register_21 (.D(Write_Data), .en(write_en_21), .Q(s5), .clk(Clock));  // open: clr
  Register #(.width(32)) register_22 (.D(Write_Data), .en(write_en_22), .Q(s6), .clk(Clock));  // open: clr
  Register #(.width(32)) register_23 (.D(Write_Data), .en(write_en_23), .Q(s7), .clk(Clock));  // open: clr
  Register #(.width(32)) register_24 (.D(Write_Data), .en(write_en_24), .Q(t8), .clk(Clock));  // open: clr
  Register #(.width(32)) register_25 (.D(Write_Data), .en(write_en_25), .Q(t9), .clk(Clock));  // open: clr
  Register #(.width(32)) register_26 (.D(Write_Data), .en(write_en_26), .Q(k0), .clk(Clock));  // open: clr
  Register #(.width(32)) register_27 (.D(Write_Data), .en(write_en_27), .Q(k1), .clk(Clock));  // open: clr
  Register #(.width(32)) register_28 (.D(Write_Data), .en(write_en_28), .Q(gp), .clk(Clock));  // open: clr
  Register #(.width(32)) register_29 (.D(Write_Data), .en(write_en_29), .Q(sp_Value), .clk(Clock));  // open: clr
  Register #(.width(32)) register_30 (.D(Write_Data), .en(write_en_30), .Q(fp), .clk(Clock));  // open: clr
  Register #(.width(32)) register_31 (.D(Write_Data), .en(write_en_31), .Q(ra_Value), .clk(Clock));  // open: clr

  // Other names for the same wires on the sheet: clk = Clock; ra[31:0] = ra_Value; read_data1[31:0] = Read_Data_1;
  //   read_data2[31:0] = Read_Data_2; read_reg1[4:0] = Read_Register_1; read_reg2[4:0] = Read_Register_2;
  //   s0[31:0] = s0_Value; s1[31:0] = s1_Value; s2[31:0] = s2_Value; sp[31:0] = sp_Value; write_en = Write_Enable;
  //   write_reg[4:0] = Write_Register

  // Notes on the sheet:
  //   INPUTS to your circuit
  //   DON'T CHANGE THE LOCATIONS OF THE INPUTS AND OUTPUTS!
  //   These are DEBUG/TEST outputs from your circuit.
  //   OUTPUTS from your circuit
endmodule
