// Logisim project regfile0.circ as structural Verilog: 1 circuit, main circuit main
module main (
  input  [1:0] Read_register_1,
  input  [1:0] Read_register_2,
  input  [1:0] write_register,
  input  [15:0] write_data,
  input  RegWrite,
  input  SetReg,
  input  clock,
  output [15:0] Reg_0_Value,
  output [15:0] Reg_1_Value,
  output [15:0] Reg_2_Value,
  output [15:0] Reg_3_Value,
  output [15:0] Read_Data_1,
  output [15:0] Read_Data_2
);

  wire E0, E1, E2, E3, or_1_out, or_2_out, or_3_out, or_4_out;

  or or_1 (or_1_out, E0, SetReg);
  or or_2 (or_2_out, E1, SetReg);
  or or_3 (or_3_out, E2, SetReg);
  or or_4 (or_4_out, E3, SetReg);
  Register #(.width(16)) Register0 (.D(write_data), .en(or_1_out), .Q(Reg_0_Value), .clk(clock));  // open: clr
  Register #(.width(16)) Register1 (.D(write_data), .en(or_2_out), .Q(Reg_1_Value), .clk(clock));  // open: clr
  Register #(.width(16)) Register2 (.D(write_data), .en(or_3_out), .Q(Reg_2_Value), .clk(clock));  // open: clr
  Register #(.width(16)) Register3 (.D(write_data), .en(or_4_out), .Q(Reg_3_Value), .clk(clock));  // open: clr
  Demultiplexer #(.select(2), .enable("false")) demultiplexer_1 (
    .out0(E0), .out1(E1), .out2(E2), .out3(E3), .in(RegWrite), .sel(write_register));
  Multiplexer #(.select(2), .width(16), .enable("false")) multiplexer_1 (
    .in0(Reg_0_Value), .in1(Reg_1_Value), .in2(Reg_2_Value), .in3(Reg_3_Value), .out(Read_Data_1),
    .sel(Read_register_1));
  Multiplexer #(.select(2), .width(16), .enable("false")) multiplexer_2 (
    .in0(Reg_0_Value), .in1(Reg_1_Value), .in2(Reg_2_Value), .in3(Reg_3_Value), .out(Read_Data_2),
    .sel(Read_register_2));

  // Other names for the same wires on the sheet: CLK = clock; R0[15:0] = Reg_0_Value; R1[15:0] = Reg_1_Value;
  //   R2[15:0] = Reg_2_Value; R3[15:0] = Reg_3_Value; RD1[15:0] = Read_Data_1; RD2[15:0] = Read_Data_2;
  //   SignRD1[1:0] = Read_register_1; SignRD2[1:0] = Read_register_2; SignWR[1:0] = write_register;
  //   WD[15:0] = write_data

  // Notes on the sheet:
  //   These are INPUTS to the circuit
  //   registers
  //   These are INPUTS to the circuit
  //   DO NOT CHANGE THE LOCATIONS OF THE INPUTS/OUTPUTS! IF YOU DO SO, YOU NEED TO MAKE SURE THE PINS ARE AT THE RIGHT PLACE!
  //   These are OUTPUTS to the circuit
  //   Yet again, the clock is not an actual clock, but an input, one that will be driven from a higher circuit
  //   Proces all control signals
  //   These are OUTPUTS to the circuit
endmodule
