// Logisim project regfile4.circ as structural Verilog: 1 circuit, main circuit main
module main (
  input  [1:0] Read_register_1,
  input  [1:0] Read_register_2,
  input  [1:0] write_register,
  input  [15:0] write_data,
  input  RegWrite,
  input  clock,
  output [15:0] Reg_0_Value,
  output [15:0] Reg_1_Value,
  output [15:0] Reg_2_Value,
  output [15:0] Reg_3_Value,
  output [15:0] Read_Data_1,
  output [15:0] Read_Data_2
);

  wire RW0, RW1, RW2, RW3;
  wire [15:0] I0, I1, I2, I3;

  Register #(.width(16)) register_1 (.D(I0), .en(RW0), .Q(Reg_0_Value), .clk(clock));  // open: clr
  Register #(.width(16)) register_2 (.D(I1), .en(RW1), .Q(Reg_1_Value), .clk(clock));  // open: clr
  Register #(.width(16)) register_3 (.D(I2), .en(RW2), .Q(Reg_2_Value), .clk(clock));  // open: clr
  Register #(.width(16)) register_4 (.D(I3), .en(RW3), .Q(Reg_3_Value), .clk(clock));  // open: clr
  Demultiplexer #(.select(2), .width(16)) demultiplexer_1 (
    .out0(I0), .out1(I1), .out2(I2), .out3(I3), .in(write_data), .sel(write_register));  // open: en
  Demultiplexer #(.select(2)) demultiplexer_2 (
    .out0(RW0), .out1(RW1), .out2(RW2), .out3(RW3), .in(RegWrite), .sel(write_register));  // open: en
  Multiplexer #(.select(2), .width(16)) multiplexer_1 (
    .in0(Reg_0_Value), .in1(Reg_1_Value), .in2(Reg_2_Value), .in3(Reg_3_Value), .out(Read_Data_1),
    .sel(Read_register_1));  // open: en
  Multiplexer #(.select(2), .width(16)) multiplexer_2 (
    .in0(Reg_0_Value), .in1(Reg_1_Value), .in2(Reg_2_Value), .in3(Reg_3_Value), .out(Read_Data_2),
    .sel(Read_register_2));  // open: en

  // Other names for the same wires on the sheet: CLK = clock; R0[15:0] = Reg_0_Value; R1[15:0] = Reg_1_Value;
  //   R2[15:0] = Reg_2_Value; R3[15:0] = Reg_3_Value; RR1[1:0] = Read_register_1; RR1OUT[15:0] = Read_Data_1;
  //   RR2[1:0] = Read_register_2; RR2OUT[15:0] = Read_Data_2; RW = RegWrite; WD[15:0] = write_data;
  //   WR[1:0] = write_register

  // Notes on the sheet:
  //   These are INPUTS to the circuit
  //   These are INPUTS to the circuit
  //   DO NOT CHANGE THE LOCATIONS OF THE INPUTS/OUTPUTS! IF YOU DO SO, YOU NEED TO MAKE SURE THE PINS ARE AT THE RIGHT PLACE!
  //   These are OUTPUTS to the circuit
  //   Yet again, the clock is not an actual clock, but an input, one that will be driven from a higher circuit
  //   These are OUTPUTS to the circuit
endmodule
