// Logisim project Fibonacci.circ as structural Verilog: 1 circuit, main circuit main
module main (
  output [7:0] out_1
);

  wire clock_1_out, clock_2_out;
  wire [7:0] adder_1_out, register_1_q;

  Register register_1 (.Q(register_1_q), .clk(clock_1_out));  // open: D, en, clr
  Clock clock_1 (.out(clock_1_out));
  Adder adder_1 (.a(register_1_q), .b(out_1), .out(adder_1_out));  // open: cin, cout
  Register register_2 (.D(adder_1_out), .Q(out_1), .clk(clock_2_out));  // open: en, clr
  Clock clock_2 (.out(clock_2_out));
endmodule
