// Logisim project MultRepeatedAdder.circ as structural Verilog: 3 circuits, main circuit main
module main (
  input  [31:0] Input_A,
  input  [31:0] Input_B,
  input  Reset,
  output [31:0] Product,
  output Stall_Pipeline
);

  wire Clock_out;

  Clock Clock (.out(Clock_out));
  Mult mult_1 (
    .A(Input_A), .B(Input_B), .Clock(Clock_out), .Reset(Reset), .Product(Product),
    .Stall_Pipeline(Stall_Pipeline));
endmodule

module Mult (
  input  [31:0] A,
  input  [31:0] B,
  input  Clock,
  input  Reset,
  output [31:0] Product,
  output Stall_Pipeline
);


  // Other names for the same wires on the sheet: clk = Clock; shouldStall = Stall_Pipeline

  // Notes on the sheet:
  //   INPUTS
  //   IMPLEMENT A*B
  //   OUTPUTS
endmodule

module CountUpTo (
  input  Reset,
  input  Clock,
  input  [31:0] Limit,
  output IsCounting
);


  // Other names for the same wires on the sheet: clk = Clock; rst = Reset

  // Notes on the sheet:
  //   INPUTS
  //   IMPLEMENT
  //   OUTPUTS
endmodule
