// Logisim project mvr17_logism_lab.circ as structural Verilog: 7 circuits, main circuit main
module main (
  input  in_1,
  input  in_2,
  input  in_3,
  input  in_4,
  input  in_5,
  input  in_6,
  input  in_7,
  input  in_8,
  input  in_9,
  input  in_10,
  input  in_11,
  input  in_12,
  input  in_13,
  input  in_14,
  input  in_15,
  output out_16,
  output out_17,
  output out_18,
  output out_19,
  output out_20,
  output [7:0] out_21,
  output [7:0] out_22
);

  AddMachine addmachine_1 (.out_1(out_21), .out_2(out_22));
  NAND nand_1 (.in_1(in_1), .in_2(in_2), .out_3(out_16));
  NOR nor_1 (.in_1(in_3), .in_2(in_4), .out_3(out_17));
  XOR xor_1 (.in_1(in_5), .in_2(in_6), .out_3(out_18));
  _2_1_MUX u_2_1_mux_1 (.x1(in_7), .Select(in_8), .x2(in_9), .out_4(out_19));
  _4_1_MUX u_4_1_mux_1 (.a(in_10), .b(in_11), .A_2(in_12), .B_2(in_13), .C(in_14), .D(in_15), .out_7(out_20));
endmodule

module NAND (
  input  in_1,
  input  in_2,
  output out_3
);

  wire and_1_out;

  and and_1 (and_1_out, in_1, in_2);
  not not_1 (out_3, and_1_out);
endmodule

module NOR (
  input  in_1,
  input  in_2,
  output out_3
);

  wire or_1_out;

  or or_1 (or_1_out, in_1, in_2);
  not not_1 (out_3, or_1_out);
endmodule

module XOR (
  input  in_1,
  input  in_2,
  output out_3
);

  wire nand_1_out_3, or_1_out;

  NAND nand_1 (.in_1(in_2), .in_2(in_1), .out_3(nand_1_out_3));
  or or_1 (or_1_out, in_1, in_2);
  and and_1 (out_3, nand_1_out_3, or_1_out);
endmodule

module _2_1_MUX (
  input  x1,
  input  Select,
  input  x2,
  output out_4
);

  wire and_1_out, and_2_out, not_1_out;

  not not_1 (not_1_out, Select);
  and and_1 (and_1_out, x1, Select);
  and and_2 (and_2_out, not_1_out, x2);
  or or_1 (out_4, and_1_out, and_2_out);
endmodule

module _4_1_MUX (
  input  a,
  input  b,
  input  A_2,
  input  B_2,
  input  C,
  input  D,
  output out_7
);

  wire and_1_out, and_2_out, and_3_out, and_4_out, not_1_out, not_2_out;

  not not_1 (not_1_out, a);
  not not_2 (not_2_out, b);
  and and_1 (and_1_out, not_1_out, A_2, not_2_out);
  and and_2 (and_2_out, a, B_2, not_2_out);
  and and_3 (and_3_out, b, C, not_1_out);
  and and_4 (and_4_out, b, D, a);
  or or_1 (out_7, and_1_out, and_2_out, and_3_out, and_4_out);
endmodule

module AddMachine (
  output [7:0] out_1,
  output [7:0] out_2
);

  wire clock_1_out;

  Adder adder_1 (.a(8'h1), .b(out_2), .out(out_1));  // open: cin, cout
  Clock clock_1 (.out(clock_1_out));
  Register register_1 (.D(out_1), .Q(out_2), .clk(clock_1_out));  // open: en, clr
endmodule
