// Logisim project logisim_lab8.circ as structural Verilog
module Ex1 (
  input  [7:0] in_1,
  output Out1,
  output [7:0] Out2
);

  and and_1 (Out1, in_1[0], in_1[7]);
  not not_1 (Out2[0], in_1[0]);

  assign Out2[7:1] = in_1[7:1];
endmodule

module rotr (
  input  [15:0] in_1,
  input  [3:0] in_2,
  output [15:0] out_3
);

  wire [15:0] multiplexer_1_out, multiplexer_2_out, multiplexer_3_out;

  Multiplexer #(.width(16), .enable("false")) multiplexer_1 (
    .in0(in_1), .in1({in_1[0], in_1[15:1]}), .out(multiplexer_1_out), .sel(in_2[0]));
  Multiplexer #(.width(16), .enable("false")) multiplexer_2 (
    .in0(multiplexer_1_out), .in1({multiplexer_1_out[1:0], multiplexer_1_out[15:2]}),
    .out(multiplexer_2_out), .sel(in_2[1]));
  Multiplexer #(.width(16), .enable("false")) multiplexer_3 (
    .in0(multiplexer_2_out), .in1({multiplexer_2_out[3:0], multiplexer_2_out[15:4]}),
    .out(multiplexer_3_out), .sel(in_2[2]));
  Multiplexer #(.width(16), .enable("false")) multiplexer_4 (
    .in0(multiplexer_3_out), .in1({multiplexer_3_out[7:0], multiplexer_3_out[15:8]}), .out(out_3),
    .sel(in_2[3]));
endmodule

module something (
  input  [15:0] A,
  input  [15:0] A_2,
  input  in_3,
  output [1:0] out_4,
  output [13:0] out_5,
  output out_6
);

  wire multiplexer_1_out;
  wire [3:1] undriven;

  Multiplexer #(.select(4), .enable("false")) multiplexer_1 (
    .in1(A[12]), .in2(A[13]), .in3(A[14]), .in4(A[15]), .in5(A[8]), .in6(A[9]), .in7(A[10]), .in8(A[11]),
    .in9(A[4]), .in10(A[5]), .in11(A[6]), .in12(A[7]), .in13(A[0]), .in14(A[1]), .in15(A[3]),
    .out(multiplexer_1_out), .sel({undriven, in_3}));  // open: in0
  // Pins of 1 and 4 bits meet at {undriven, in_3}

  assign A[2] = A[3];
  assign out_4 = A_2[1:0];
  assign out_5 = A_2[15:2];
endmodule
