// Logisim project ALU.circ as structural Verilog: 2 circuits, main circuit ALU
// LAB12-ALU
module ALU (
  input  [31:0] ALU_Source_1,
  input  [31:0] ALU_Source_2,
  input  [2:0] ALU_Control,
  output [31:0] ALU_Result
);

  wire [4:0] bit_extender_1_out, bit_extender_2_out, bit_extender_3_out, bit_extender_4_out,
       bit_extender_5_out;
  wire [31:0] AND, OR, rotate_left, rotate_right, sArthR, sll, slr, XOR;

  // Probe on ALU_Source_1
  // Probe on ALU_Source_2
  Bit_Extender #(.in_width(32), .out_width(5)) bit_extender_1 (.in(ALU_Source_2), .out(bit_extender_1_out));
  Bit_Extender #(.in_width(32), .out_width(5)) bit_extender_2 (.in(ALU_Source_2), .out(bit_extender_2_out));
  Bit_Extender #(.in_width(32), .out_width(5)) bit_extender_3 (.in(ALU_Source_2), .out(bit_extender_3_out));
  Bit_Extender #(.in_width(32), .out_width(5)) bit_extender_4 (.in(ALU_Source_2), .out(bit_extender_4_out));
  Bit_Extender #(.in_width(32), .out_width(5)) bit_extender_5 (.in(ALU_Source_2), .out(bit_extender_5_out));
  assign AND = ALU_Source_1 & ALU_Source_2;  // AND_Gate and_1, 32 bits wide
  Shifter #(.width(32)) shifter_1 (.in(ALU_Source_1), .\dist (bit_extender_1_out), .out(sll));
  Shifter #(.width(32), .shift("lr")) shifter_2 (.in(ALU_Source_1), .\dist (bit_extender_2_out), .out(slr));
  Shifter #(.width(32), .shift("ar")) shifter_3 (.in(ALU_Source_1), .\dist (bit_extender_3_out), .out(sArthR));
  Shifter #(.width(32), .shift("rl")) shifter_4 (.in(ALU_Source_1), .\dist (bit_extender_4_out), .out(rotate_left));
  Shifter #(.width(32), .shift("rr")) shifter_5 (.in(ALU_Source_1), .\dist (bit_extender_5_out), .out(rotate_right));
  assign XOR = ALU_Source_1 ^ ALU_Source_2;  // XOR_Gate xor_1, 32 bits wide
  assign OR = ALU_Source_1 | ALU_Source_2;  // OR_Gate or_1, 32 bits wide
  // Probe on ALU_Result
  Multiplexer #(.select(3), .width(32), .enable("false")) multiplexer_1 (
    .in0(sll), .in1(slr), .in2(sArthR), .in3(rotate_left), .in4(rotate_right), .in5(AND), .in6(OR),
    .in7(XOR), .out(ALU_Result), .sel(ALU_Control));
  // Probe on ALU_Control

  // Other names for the same wires on the sheet: control[2:0] = ALU_Control; result[31:0] = ALU_Result;
  //   source1[31:0] = ALU_Source_1; source2[31:0] = ALU_Source_2

  // Notes on the sheet:
  //   DO NOT CROSS WIRES
  //   OVER THIS BOX
  //   DO NOT CROSS WIRES
  //   OVER THIS BOX
  //   COMPUTE ALL POSSIBLE OPERATIONS
  //   DO NOT CROSS WIRES
  //   OVER THIS BOX
  //   DO NOT CROSS WIRES
  //   OVER THIS BOX
  //   SELECT THE REQUESTED RESULT
endmodule

module REC_work (
  input  Source_1,
  input  Source_1_2,
  input  [7:0] Source_1_3,
  input  [7:0] Source_1_4,
  input  [7:0] Source_1_5,
  output out_6
);

  wire and_1_out, clock_1_out, or_1_out;
  wire [7:0] adder_1_out, multiplier_1_out;

  and and_1 (and_1_out, Source_1_2, Source_1);
  or or_1 (or_1_out, Source_1_2, Source_1);
  Multiplier multiplier_1 (.a(Source_1_3), .b(Source_1_5), .out(multiplier_1_out));  // open: cin, cout
  and and_2 (out_6, and_1_out, or_1_out);
  Adder adder_1 (.a(multiplier_1_out), .b(Source_1_4), .out(adder_1_out));  // open: cin, cout
  Clock clock_1 (.out(clock_1_out));
  Register register_1 (.D(adder_1_out), .Q(Source_1_4), .clk(clock_1_out));  // open: en, clr

  // Notes on the sheet:
  //   30 ns
  //   40 ns
  //   1 cycle/70 ns
  //   1 Hz = 1 cycle/sec
endmodule
